# Fritzing sketch VacuumATM (saved by Fritzing 1.0.1rc)
circuit board: 8.46667cm x 5.64444cm
breadboards: 1

parts:
  A1 = Particle - Photon2
  NEOPIXEL1 = Neopixel Strip -- Black (30/m)
  M1 = Dagu DGServo 9g (Top view) [part_number=RS001B]
  S1 = Pushbutton [package="[THT]"]

nets:
  3.3V: A1.Pin_2, M1.vcc, S1.Pin_1, S1.Pin_2
  GND: A1.Pin_4, NEOPIXEL1.GND, M1.gnd
  N1: A1.Pin_7, S1.Pin_3, S1.Pin_4
  N2: A1.Pin_8, M1.pulse
  N3: A1.Pin_19, NEOPIXEL1.Din
  N4: A1.Pin_26, NEOPIXEL1.+5V

custom parts:
  Particle - Photon2: The Photon 2 is a microcontroller and Wi-Fi networking developed by particle. Features: 802.11a/b/g/n Wi-Fi, 2.4 GHz and 5 GHz Integrated PCB antenna Integrated U.FL connector for external antenna Integrated RF switch BLE 5 using same antenna as Wi-Fi Realtek RTL8721DM MCU ARM Cortex M33 CPU, 200 MHz 2048 KB (2 MB) user application maximum size 3072 KB (3 MB) of RAM available to user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
  Neopixel Strip -- Black (30/m): These NeoPixel strips have 30 digitally-addressable pixel LEDs per meter and are very affordable and are only 12.5 mm wide, 10 mm if you remove the strip from the casing.
  Pushbutton: A generic pushbutton.
